# Fritzing sketch rf (saved by Fritzing 0.8.7b)
circuit board: 8.46667cm x 5.64444cm

parts:
  Part1 = Arduino Nano (Rev3.0)
  J1 = female pin header, 2 pins [form="♀ (female)"]
  J2 = female pin header, 2 pins [form="♀ (female)"]
  J3 = female pin header, 2 pins [form="♀ (female)"]
  J5 = female pin header, 2 pins [form="♀ (female)"]
  LED1 = LED - 5mm [color="Red (633nm)" package="5 mm [THT]"]  # not connected
  J6 = Piezo Speaker
  LED2 = LED - 5mm [color="Red (633nm)" package="5 mm [THT]"]
  J7 = female pin header, 2 pins [form="♀ (female)"]
  J8 = female pin header, 2 pins [form="♀ (female)"]
  J9 = female pin header, 2 pins [form="♀ (female)"]
  R1 = Resistor [tolerance=±5% resistance=220 package=THT]
  R2 = Resistor [tolerance=±5% resistance=220 package=THT]
  J10 = female pin header, 2 pins [form="♀ (female)"]
  J11 = female pin header, 2 pins [form="♀ (female)"]
  J12 = female pin header, 2 pins [form="♀ (female)"]
  J13 = female pin header, 2 pins [form="♀ (female)"]
  J14 = female pin header, 2 pins [form="♀ (female)"]
  J15 = female pin header, 2 pins [form="♀ (female)"]
  J16 = female pin header, 2 pins [form="♀ (female)"]
  J17 = female pin header, 2 pins [form="♀ (female)"]
  J18 = female pin header, 2 pins [form="♀ (female)"]
  J19 = female pin header, 2 pins [form="♀ (female)"]
  J20 = female pin header, 2 pins [form="♀ (female)"]
  J21 = female pin header, 2 pins [form="♀ (female)"]

nets:
  N1: Part1.GND, J3.pin2, J6.pin1, J7.pin2, J9.pin2, J12.pin2, J14.pin1, J18.pin1
  N2: Part1.D2, J6.pin2, J7.pin1
  N3: Part1.D3, J15.pin2
  N4: Part1.D4, R1.Pin_1
  N5: Part1.D5, J11.pin1
  N6: Part1.D6, J10.pin2
  N7: Part1.D7, J1.pin1
  N8: Part1.D8, J1.pin2
  N9: Part1.D9, J5.pin2, J17.pin2
  N10: Part1.D10, J16.pin1
  N11: Part1.D11/MOSI, J2.pin2, J19.pin1
  N12: Part1.D12/MISO, J3.pin1, J18.pin2
  N13: Part1.5V, J10.pin1, J14.pin2
  N14: Part1.A5, J13.pin1, J21.pin1
  N15: Part1.A4, J13.pin2, J21.pin2
  N16: Part1.A0, R2.Pin_1
  N17: Part1.3V3, J5.pin1, J12.pin1, J17.pin1, J20.pin1
  N18: Part1.D13/SCK, J2.pin1, J19.pin2
  N19: LED2.cathode, J8.pin2

notes:
  sonar (distance sensor)
  servo motors 2
  oled
  rfid 2
  IR thermal
